# Fritzing sketch Linear Actuator Circuit (saved by Fritzing 0.9.3b)
breadboards: 1

parts:
  L298N1 = L298N DC motor driver
  Raspberry_Pi_1 = Raspberry Pi 3 [part_number=RPI-3-V1.2]
  VCC1 = Battery block 9V
  M1 = linear actuator [package=THT]

nets:
  N1: L298N1.OUT1, M1.pin1
  N2: L298N1.OUT2, M1.pin2
  N3: L298N1.12V, VCC1.+
  GND: L298N1.GND, Raspberry_Pi_1.GND, VCC1.-
  N4: L298N1.IN1, Raspberry_Pi_1.GIPO25
  N5: L298N1.IN2, Raspberry_Pi_1.GIPO8

custom parts:
  L298N DC motor driver: 2x DC motor driver with 78M05 positive voltage regulator (7..35 V) L298N: max 46 V, 2 A Set 5 V Enable jumper to enable 5 V regultor (needed for the L298N) and +5 V output at screw terminal or supply external +5 V at screw terminal Set ENA and/or ENB to +5 V to enable motor permanently or supply ENA and/or ENB with PWM signal IN1 and IN2 set rotation directory for motor A (OUT1/OUT2) IN2 and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
  linear actuator: Generic linear actuator.
