# Fritzing sketch Ultrasonic Circuit (saved by Fritzing 0.9.3b)
breadboards: 1

parts:
  HC-SR04_Sensor_1 = HC-SR04 Ultrasonic Distance Sensor
  HC-SR04_Sensor_2 = HC-SR04 Ultrasonic Distance Sensor
  Part1 = Logic Level Converter
  Raspberry_Pi_1 = Raspberry Pi 3 [part_number=RPI-3-V1.2]

nets:
  VCC: HC-SR04_Sensor_1.VCC, HC-SR04_Sensor_2.VCC, Raspberry_Pi_1.5V
  N1: HC-SR04_Sensor_1.TRIG, Raspberry_Pi_1.GIPO21
  N2: HC-SR04_Sensor_1.ECHO, Part1.TX2_HV
  GND: HC-SR04_Sensor_1.GND, HC-SR04_Sensor_2.GND, Part1.GND, Raspberry_Pi_1.GND
  N3: HC-SR04_Sensor_2.TRIG, Raspberry_Pi_1.GPIO2
  N4: HC-SR04_Sensor_2.ECHO, Part1.TX_HV
  N5: Part1.TX2_LV, Raspberry_Pi_1.GIPO20
  N6: Part1.TX_LV, Raspberry_Pi_1.GIPO8
